# Fritzing sketch 3D_Compass (saved by Fritzing 0.9.1b)

parts:
  Part1 = Arduino Uno (Rev3)
  R1 = Resistor [tolerance=±5% resistance=330 package=THT]
  C1 = Electrolytic Capacitor [capacitance=1mF package="100 mil [THT, electrolytic]"]
  neopixel1 = Neopixel Ring 16
  neopixel2 = Neopixel 24 Ring
  BREAKOUT1 = HMC5883L Compass Breakout

nets:
  N1: Part1.A4/SDA, BREAKOUT1.SDA
  N2: Part1.A5/SCL, BREAKOUT1.SCL
  N3: Part1.D13/SCK, R1.Pin_0
  GND: Part1.GND, C1.-, neopixel1.GND, neopixel2.GND, BREAKOUT1.GND
  N4: Part1.3V3, BREAKOUT1.3vo
  VCC: Part1.5V, C1.+, neopixel1.VCC, neopixel2.Vcc
  N5: R1.Pin_1, neopixel2.IN
  N6: neopixel1.IN, neopixel2.OUT

notes:
  300-500 Ohm Resistor as a current limiter on the data line
  1000 µF Capacitor to buffer neo-pixel spikes

custom parts:
  Neopixel Ring 16: Neopixel Ring x16
